// Logisim project matrix.circ as structural Verilog: 1 circuit, main circuit main
module main (
  input  [3:0] IR,
  input  [2:0] Flags,
  input  DMA
);

  wire clock_1_out, Reset_out;
  wire [3:0] undriven;
  wire [7:0] rom_1_data, rom_2_data;
  wire [12:0] bit_extender_1_out;

  Register #(.width(4)) register_1 (.D(undriven), .en(1'b1), .Q(rom_1_data[3:0]), .clk(clock_1_out), .clr(Reset_out));
  Clock clock_1 (.out(clock_1_out));
  ROM #(.addrWidth(13)) rom_1 (.addr({1'b0, IR, Flags, DMA, undriven}), .data(rom_1_data), .sel(1'b1));
  Button Reset (.out(Reset_out));
  assign bit_extender_1_out = {{9{1'b0}}, undriven};  // Bit_Extender bit_extender_1
  ROM #(.addrWidth(13)) rom_2 (.addr(bit_extender_1_out), .data(rom_2_data), .sel(1'b1));
  LED Ctrl_ALU_Enable_I (.in(rom_1_data[7]));
  LED Ctrl_PC_Output_I (.in(rom_1_data[6]));
  LED Ctrl_PC_Input_I (.in(rom_1_data[5]));
  LED Ctrl_PC_Count (.in(rom_1_data[4]));
  LED Ctrl_Mem_W (.in(rom_2_data[0]));
  LED Ctrl_Mem_R (.in(rom_2_data[1]));
  LED Ctrl_MAR_Output_I (.in(rom_2_data[2]));
  LED Ctrl_MAR_High_Input_I (.in(rom_2_data[3]));
  LED Ctrl_MAR_Low_Input_I (.in(rom_2_data[4]));
  LED Ctrl_IR_Input_I (.in(rom_2_data[5]));
  LED Ctrl_ACC_Input_I (.in(rom_2_data[6]));
  LED Ctrl_ACC_Output_I (.in(rom_2_data[7]));
endmodule
